# Fritzing sketch hani-mandl-wiring_v1undv2 (saved by Fritzing 0.9.4)

parts:
  S7 = Pushbutton [package=THT]  # not connected
  S8 = Pushbutton [package=THT]  # not connected
  R3 = Rotary Potentiometer (Small) [maximum_resistance=100kΩ package=THT]  # not connected
  kleiner_Servo_nur_Testbetrieb = Basic Servo
  S9 = Toggle Switch [package=THT]  # not connected
  Bauteil3 = HX711 Weighing Sensor Module

nets:
  GND: kleiner_Servo_nur_Testbetrieb.gnd, Bauteil3.GND

notes:
  New Heltec Wifi Kit 32 (V2)
