# Fritzing sketch hani-mandl-wiring_corresponding-to-code-v0.1.3_v0.1 (saved by Fritzing 0.9.3b)
breadboards: 1

parts:
  J4 = female pin header, 18 pins [form="♀ (female)"]
  J5 = female pin header, 18 pins [form="♀ (female)"]
  S4 = Pushbutton [package=THT]
  S5 = Pushbutton [package=THT]
  R2 = Rotary Potentiometer (Small) [maximum_resistance=100kΩ package=THT]
  Bauteil2 = HX711 Weighing Sensor Module
  J6 = Basic Servo
  S6 = Toggle Switch [package=THT]

nets:
  N1: J4.pin3, S6.COM
  N2: J4.pin5, S5.leg0
  N3: J4.pin6, S4.leg0
  N4: J4.pin7, S6.L2
  N5: J4.pin8, S6.L1
  N6: J4.pin15, R2.wiper
  GND: J5.pin1, R2.leg1, Bauteil2.GND, J6.gnd
  N7: J5.pin2, J6.vcc
  N8: J5.pin3, S4.leg1, S5.leg1, R2.leg2, Bauteil2.VCC
  N9: J5.pin8, J6.pulse
  N10: J5.pin12, Bauteil2.DO/RX
  N11: J5.pin13, Bauteil2.CK/TX
