# Fritzing sketch hani-mandl-wiring_corresponding-to-code-v0.1.4_v0.2.0 (saved by Fritzing 0.9.3b)
breadboards: 1

parts:
  J4 = female pin header, 18 pins [form="♀ (female)"]
  J5 = female pin header, 18 pins [form="♀ (female)"]
  S4 = Pushbutton [package=THT]
  S5 = Pushbutton [package=THT]
  R2 = Rotary Potentiometer (Small) [maximum_resistance=100kΩ package=THT]
  Bauteil2 = HX711 Weighing Sensor Module
  J6 = Basic Servo
  S6 = Toggle Switch [package=THT]

nets:
  N1: J4.pin1, R2.leg2
  N2: J4.pin3, R2.leg1
  N3: J4.pin5, S4.leg0
  N4: J4.pin6, S4.leg1
  N5: J4.pin7, S5.leg0
  N6: J4.pin8, S5.leg1
  N7: J4.pin15, R2.wiper
  N8: J5.pin1, J6.gnd
  N9: J5.pin2, J6.vcc
  N10: J5.pin3, Bauteil2.VCC
  N11: J5.pin4, Bauteil2.GND
  N12: J5.pin8, J6.pulse
  N13: J5.pin12, Bauteil2.CK/TX
  N14: J5.pin13, Bauteil2.DO/RX
  N15: J5.pin16, S6.L1
  N16: J5.pin17, S6.COM
  N17: J5.pin18, S6.L2
