# Fritzing sketch hani-mandl-wiring_esp32_v0.2_experimental (saved by Fritzing 0.9.3b)

parts:
  Bauteil3 = HX711 Weighing Sensor Module
  S9 = Toggle Switch [package=THT]
  J2 = Basic Servo
  S10 = Round Pushbutton
  S11 = Round Pushbutton
  J1 = Piezo Speaker
  SW1 = ENCODER_RGB_CA [package=encoder_led_3]
  Power_plug1 = Power plug  # not connected
  U1 = ESP32-38PinWide [part_number=ESP32-38PinWide]
  Bauteil4 = SPI OLED Monochrome 128x64 0.96 inch

nets:
  VCC: Bauteil3.VCC, SW1.+, U1.3.3, Bauteil4.VDD
  GND: Bauteil3.GND, J1.pin1, SW1.-B, U1.GND, Bauteil4.GND
  N1: Bauteil3.DO/RX, U1.GPIO5
  N2: Bauteil3.CK/TX, U1.GPIO17
  N3: S9.L1, U1.GPIO23
  N4: S9.COM, U1.GPIO19
  N5: S9.L2, U1.GPIO22
  N6: J2.pulse, U1.GPIO2
  N7: S10.leg0, U1.GPIO14
  N8: S10.leg1, U1.GPIO27
  N9: S11.leg0, U1.GPIO13
  N10: S11.leg1, U1.GPIO12
  N11: J1.pin2, U1.GPIO25
  N12: SW1.A, U1.GPIO32
  N13: SW1.B, U1.GPIO33
  N14: SW1.C, U1.GPIO26
  N15: U1.GPIO15, Bauteil4.CS
  N16: U1.GPIO4, Bauteil4.SDA
  N17: U1.GPIO16, Bauteil4.RES
  N18: U1.GPIO18, Bauteil4.SCK
  N19: U1.GPIO21, Bauteil4.DC

notes:
  5 V max.

custom parts:
  Round Pushbutton: A generic pushbutton.
  ESP32-38PinWide: Generic 38-Pin ESP32 with wide format (only access to one side of pins on a breadboard) based on Stephen Lilley's HiLetgo ESP-WROOM-32 ESP32 ESP-32S Development Board.
  SPI OLED Monochrome 128x64 0.96 inch: Unknown 128x64 0.96 inch 128x64 SPI Monochrome OLED display
