# Fritzing sketch hani-mandl-wiring_heltec_v0.5_usb (saved by Fritzing 0.9.3b)

parts:
  Bauteil3 = HX711 Weighing Sensor Module
  S9 = Toggle Switch [package=THT]
  Mod1 = Heltec WiFi Kit 32 [part_number=HTIT-WB32LA]
  J2 = Basic Servo
  S10 = Round Pushbutton
  S11 = Round Pushbutton
  J1 = Piezo Speaker
  SW1 = ENCODER_RGB_CA [package=encoder_led_3]
  USBTTL1 = USB TTL Serial Cable  # not connected

nets:
  N1: Bauteil3.VCC, Mod1.pin_16, Mod1.pin_21, SW1.+
  GND: Bauteil3.GND, Mod1.pin_15, Mod1.pin_18, Mod1.pin_19, J2.gnd, J1.pin1, SW1.-B
  N2: Bauteil3.DO/RX, Mod1.pin_6
  N3: Bauteil3.CK/TX, Mod1.pin_7
  N4: S9.L1, Mod1.pin_4
  N5: S9.COM, Mod1.pin_3
  N6: S9.L2, Mod1.pin_2
  N7: Mod1.pin_11, J2.pulse
  N8: Mod1.pin_17, Mod1.pin_20, J2.vcc
  N9: Mod1.pin_23, S11.leg1
  N10: Mod1.pin_24, S11.leg0
  N11: Mod1.pin_25, S10.leg1
  N12: Mod1.pin_26, S10.leg0
  N13: Mod1.pin_27, SW1.C
  N14: Mod1.pin_28, J1.pin2
  N15: Mod1.pin_29, SW1.B
  N16: Mod1.pin_30, SW1.A

notes:
  beim Heltec-Version 1 kann alternativ auch diese GND-Verbindung genutzt werden

custom parts:
  Heltec WiFi Kit 32: Heltec WiFi Kit 32 WiFi Kit 32 is a classic IoT dev-board designed & produced by Heltec Automation(TM). It’s a highly integrated product based on ESP32 + SX127x, it has Wi-Fi, BLE, LoRa functions, also Li-Po battery management system, 0.96″ OLED are also included. It’s the best choice for smart cities, smart farms, smart home, and IoT makers.
  Round Pushbutton: A generic pushbutton.
