# Fritzing sketch hani-mandl-wiring_rotary (saved by Fritzing 0.9.4)

parts:
  S7 = Pushbutton [package=THT]
  S8 = Pushbutton [package=THT]
  S9 = Toggle Switch [package=THT]
  Bauteil3 = HX711 Weighing Sensor Module
  SW1 = ENCODER_RGB_CA [package=encoder_led_3]
  Mod1 = Heltec WiFi Kit 32 V2 [part_number=HTIT-WB32LA]
  Kleiner_Servo_nur_Testbetrieb! = Basic Servo

nets:
  N1: S7.leg0, Mod1.pin_23
  N2: S7.leg1, Mod1.pin_24
  N3: S8.leg0, Mod1.pin_25
  N4: S8.leg1, Mod1.pin_26
  N5: S9.L1, Mod1.pin_4
  N6: S9.COM, Mod1.pin_3
  N7: S9.L2, Mod1.pin_2
  N8: Bauteil3.VCC, Mod1.pin_16, Mod1.pin_20
  GND: Bauteil3.GND, SW1.-B, Mod1.pin_18, Mod1.pin_19, Kleiner_Servo_nur_Testbetrieb!.gnd
  N9: Bauteil3.DO/RX, Mod1.pin_6
  N10: Bauteil3.CK/TX, Mod1.pin_7
  N11: SW1.+, Mod1.pin_21
  N12: SW1.A, Mod1.pin_30
  N13: SW1.B, Mod1.pin_29
  N14: SW1.C, Mod1.pin_27
  N15: Mod1.pin_11, Kleiner_Servo_nur_Testbetrieb!.pulse
  N16: Mod1.pin_17, Kleiner_Servo_nur_Testbetrieb!.vcc

custom parts:
  Heltec WiFi Kit 32 V2: Heltec WiFi Kit 32 V2 - updated Layout WiFi Kit 32 is a classic IoT dev-board designed & produced by Heltec Automation(TM). It’s a highly integrated product based on ESP32 + SX127x, it has Wi-Fi, BLE, LoRa functions, also Li-Po battery management system, 0.96″ OLED are also included. It’s the best choice for smart cities, smart farms, smart home, and IoT makers.
